# Fritzing sketch controller (saved by Fritzing 0.9.3b)
breadboards: 1

parts:
  Arduino = Arduino Due (Rev2b)
  Light = Square Pushbutton
  Joystick_1 = Thumb Joystick
  Joystick_2 = Thumb Joystick
  2/16 = Square Pushbutton
  2/17 = Square Pushbutton
  2/18 = Square Pushbutton
  2/19 = Square Pushbutton
  Front_Hydraulic = Taiway 100-SP-X-T1 SPDT Miniature Toggle Switch [part_number=100-SP-X-T1-0-0-B1-M1 package=THT]
  Back_Hydraulic = Taiway 100-SP-X-T1 SPDT Miniature Toggle Switch [part_number=100-SP-X-T1-0-0-B1-M1 package=THT]
  Engine_Start = Square Pushbutton
  Workinglight_Front = Square Pushbutton
  Warning_Light = Square Pushbutton
  Working_Light_Back = Square Pushbutton
  Diff_Front = Square Pushbutton
  All_Wheel_Drive = Square Pushbutton
  Diff_Back = Square Pushbutton
  Helper = Square Pushbutton
  Engine_Key = Taiway 100-SP-X-T1 SPDT Miniature Toggle Switch [part_number=100-SP-X-T1-0-0-B1-M1 package=THT]  # not connected
  2/3 = Square Pushbutton
  2/1 = Square Pushbutton
  2/4 = Square Pushbutton
  2/2 = Square Pushbutton
  2/7 = Square Pushbutton
  2/9 = Square Pushbutton
  2/8 = Square Pushbutton
  2/6 = Square Pushbutton
  Handbrake = Square Pushbutton
  2/20 = Square Pushbutton
  2/10 = Square Pushbutton
  2/5 = Square Pushbutton
  2/11 = Square Pushbutton
  2/13 = Square Pushbutton
  2/14 = Square Pushbutton
  2/15 = Square Pushbutton
  2/12 = Square Pushbutton
  1/15_&_1/16 = Taiway 100-SP-X-T1 SPDT Miniature Toggle Switch [part_number=100-SP-X-T1-0-0-B1-M1 package=THT]
  1/17_&_1/18 = Taiway 100-SP-X-T1 SPDT Miniature Toggle Switch [part_number=100-SP-X-T1-0-0-B1-M1 package=THT]
  2/21_&_2/22 = Taiway 100-SP-X-T1 SPDT Miniature Toggle Switch [part_number=100-SP-X-T1-0-0-B1-M1 package=THT]
  Joystick_3 = Thumb Joystick
  Joystick_4 = Thumb Joystick
  1/21 = Square Pushbutton
  1/25 = Square Pushbutton
  2/27 = Square Pushbutton
  2/25 = Square Pushbutton
  1/23 = Square Pushbutton
  2/26 = Square Pushbutton
  2/28 = Square Pushbutton
  1/26 = Square Pushbutton
  1/24 = Square Pushbutton
  1/22 = Square Pushbutton
  2/29 = Square Pushbutton
  2/30 = Square Pushbutton

nets:
  N1: Arduino.A0, Joystick_1.VERT
  N2: Arduino.A1, Joystick_1.HORZ
  N3: Arduino.A2, Joystick_2.VERT
  N4: Arduino.A3, Joystick_2.HORZ
  N5: Arduino.A4, Joystick_3.VERT
  N6: Arduino.A5, Joystick_3.HORZ
  N7: Arduino.A6, Joystick_4.VERT
  N8: Arduino.A7, Joystick_4.HORZ
  VCC: Arduino.5V, Joystick_1.VCC, Joystick_2.VCC, Joystick_3.VCC, Joystick_4.VCC
  GND: Arduino.GND, Joystick_1.GND, Joystick_2.GND, 1/15_&_1/16.COM, Joystick_3.GND, Joystick_4.GND
  N9: Arduino.D22, Front_Hydraulic.COM, Back_Hydraulic.COM
  N10: Arduino.D23, Light.leg1, Front_Hydraulic.L2, Workinglight_Front.leg1, Diff_Front.leg1
  N11: Arduino.D24, Diff_Front.leg0, All_Wheel_Drive.leg0, Diff_Back.leg0, Handbrake.leg0
  N12: Arduino.D25, Front_Hydraulic.L1, Engine_Start.leg1, Warning_Light.leg1, All_Wheel_Drive.leg1
  N13: Arduino.D26, Light.leg0, Engine_Start.leg0, Working_Light_Back.leg0, Helper.leg0
  N14: Arduino.D27, Back_Hydraulic.L2, Helper.leg1, Handbrake.leg1
  N15: Arduino.D28, Workinglight_Front.leg0, Warning_Light.leg0
  N16: Arduino.D29, Back_Hydraulic.L1, Working_Light_Back.leg1, Diff_Back.leg1
  N17: Arduino.D30, 1/15_&_1/16.L1
  N18: Arduino.D31, 1/15_&_1/16.L2
  N19: Arduino.D32, 1/17_&_1/18.L1
  N20: Arduino.D33, 1/17_&_1/18.L2
  N21: Arduino.D34, 2/21_&_2/22.L1
  N22: Arduino.D35, 2/21_&_2/22.L2
  N23: Arduino.D36, Joystick_1.SEL
  N24: Arduino.D37, Joystick_2.SEL
  N25: Arduino.D38, Joystick_3.SEL
  N26: Arduino.D39, Joystick_4.SEL
  N27: Arduino.D42, 2/29.leg1, 2/30.leg1
  N28: Arduino.D43, 2/3.leg0, 2/1.leg0, 2/4.leg0, 2/2.leg0, 2/5.leg0
  N29: Arduino.D44, 2/20.leg1, 2/10.leg1, 2/5.leg1, 2/15.leg1, 2/27.leg1, 2/28.leg1
  N30: Arduino.D45, 2/7.leg0, 2/9.leg0, 2/8.leg0, 2/6.leg0, 2/10.leg0
  N31: Arduino.D46, 2/19.leg1, 2/4.leg1, 2/9.leg1, 2/14.leg1, 2/25.leg1, 2/26.leg1
  N32: Arduino.D47, 2/11.leg0, 2/13.leg0, 2/14.leg0, 2/15.leg0, 2/12.leg0
  N33: Arduino.D48, 2/18.leg1, 2/3.leg1, 2/8.leg1, 2/13.leg1, 1/25.leg1, 1/26.leg1
  N34: Arduino.D49, 2/16.leg0, 2/17.leg0, 2/18.leg0, 2/19.leg0, 2/20.leg0
  N35: Arduino.D50, 2/17.leg1, 2/2.leg1, 2/7.leg1, 2/12.leg1, 1/23.leg1, 1/24.leg1
  N36: Arduino.D51, 1/21.leg0, 1/25.leg0, 2/27.leg0, 2/25.leg0, 1/23.leg0, 2/29.leg0
  N37: Arduino.D52, 2/16.leg1, 2/1.leg1, 2/6.leg1, 2/11.leg1, 1/21.leg1, 1/22.leg1
  N38: Arduino.D53, 2/26.leg0, 2/28.leg0, 1/26.leg0, 1/24.leg0, 1/22.leg0, 2/30.leg0
  N39: 1/17_&_1/18.COM, 2/21_&_2/22.COM
